# Fritzing sketch Circuit (saved by Fritzing 0.9.5d)
breadboards: 1

parts:
  Part1 = Arduino Mega ADK (Rev3)
  M2 = ESC
  920KV_Motor2 = DJI 920 KV Motor
  M3 = ESC
  920KV_Motor3 = DJI 920 KV Motor
  M4 = ESC
  920KV_Motor4 = DJI 920 KV Motor
  M5 = ESC
  920KV_Motor5 = DJI 920 KV Motor
  Power_plug3 = Power plug  # not connected

nets:
  N1: Part1.D11_PWM, M5.DATA
  N2: Part1.D10_PWM, M4.DATA
  N3: Part1.D9_PWM, M2.DATA
  N4: Part1.D8_PWM, M3.DATA
  GND: Part1.GND, M2.GND, M3.GND, M4.GND, M5.GND
  N5: M2.U, 920KV_Motor2.u
  N6: M2.V, 920KV_Motor2.v
  N7: M2.W, 920KV_Motor2.w
  N8: M3.U, 920KV_Motor3.u
  N9: M3.V, 920KV_Motor3.v
  N10: M3.W, 920KV_Motor3.w
  N11: M4.U, 920KV_Motor4.u
  N12: M4.V, 920KV_Motor4.v
  N13: M4.W, 920KV_Motor4.w
  N14: M5.U, 920KV_Motor5.u
  N15: M5.V, 920KV_Motor5.v
  N16: M5.W, 920KV_Motor5.w

notes:
  BLDC
  ESC
  ADAPTER INPUT
  11.1v LiPO Battery

custom parts:
  DJI 920 KV Motor: DJI Brushless Outrunner 2212/920K Motor F330-550
